# Fritzing sketch arduinoDrawing (saved by Fritzing 0.9.3b)
breadboards: 1

parts:
  Mod1 = Arduino MKR Wifi 1010
  R1 = Resistor [tolerance=±5% resistance=220 package=THT]
  LED1 = LED - 5mm [color="Red (633nm)" package="5 mm [THT]"]
  R2 = Resistor [tolerance=±5% resistance=10k package=THT]
  R3 = Photocell (LDR) [package=THT]
  R4 = Resistor [tolerance=±5% resistance=220 package=THT]
  PIR2 = PIR sensor
  DHT1 = DHT22 Humidity and Temperature Sensor
  DHT2 = DHT22 Humidity and Temperature Sensor
  FC-1 = Sound Sensor
  LED2 = LED - 5mm [color="Red (633nm)" package="5 mm [THT]"]
  LED3 = LED - 5mm [color="Red (633nm)" package="5 mm [THT]"]
  Driver1 = 28BYJ-48 Driver Module [part_number=ULN2003 package=THT]
  SM1 = 28BYJ-48 Stepper Motor [part_number=28BYJ-48]
  R5 = Resistor [tolerance=±5% resistance=220 package="0603 [SMD]"]
  R6 = Resistor [tolerance=±5% resistance=220 package="1206 [SMD]"]

nets:
  GND: Mod1.GND, LED1.cathode, R2.Pin_0, R4.Pin_0, PIR2.GND, DHT1.GND, DHT2.GND, FC-1.GND, LED2.cathode, LED3.cathode, Driver1.GND
  N1: Mod1.A1, DHT1.DATA
  N2: Mod1.A2, Driver1.IN2
  N3: Mod1.A3, FC-1.OUT
  N4: Mod1.A4, R5.Pin_0
  N5: Mod1.A5, PIR2.SIG
  N6: Mod1.A6, R3.pin_0, R4.Pin_1
  N7: Mod1.D0, DHT2.DATA
  N8: Mod1.D1, R1.Pin_0
  N9: Mod1.~D2, R6.Pin_1
  N10: Mod1.~D3, Driver1.IN3
  N11: Mod1.~D4, Driver1.IN1
  N12: Mod1.~D5, Driver1.IN4
  VDD: Mod1.+5V, R3.pin_1, PIR2.VDD, DHT1.VDD, DHT2.VDD, FC-1.VCC, Driver1.Vmotor
  N13: R1.Pin_1, LED1.anode
  N14: LED2.anode, R6.Pin_0
  N15: LED3.anode, R5.Pin_1
  N16: Driver1.blue-pin, SM1.blue-pin
  N17: Driver1.pink-pin, SM1.pink-pin
  N18: Driver1.yellow-pin, SM1.yellow-pin
  N19: Driver1.orange-pin, SM1.orange-pin
  N20: Driver1.red-pin, SM1.red-pin

custom parts:
  Arduino MKR Wifi 1010: Arduino MKR Wifi 1010, SAMD21 Cortex-M0+ 32bit Low Power ARM MCU,Flash Memory 256 KB, SRAM 32KB, 48mhz clock, Ublok Wifi interface.
  28BYJ-48 Driver Module: ULN2003 Driver Module for the 28BYJ-48 Unipolar Stepper Motor LED A - Blue wire - Bottom coil left LED B - Pink wire - Top coil left LED C - Yellow wire - Bottom coil right LED D - Orange wire - Top coil right Common rail - red Connector pins: blue - pink - yellow - orange - red Control pins - IN1 to IN4 Power pins - GND & Vmotor (5-12V) On/Off jumper (if removed, power to motor is cut).
  28BYJ-48 Stepper Motor: Unipolar Stepper Motor 28BYJ-48 Top coil - pink & orange Bottom coil - blue & yellow Common rail - red Connector pins: blue - pink - yellow - orange - red
